# Fritzing sketch PricehaxBT_IRDongle_project (saved by Fritzing 0.9.3b)
circuit board: 4.1cm x 7.70019cm
breadboards: 1

parts:
  HC-05_/_HC-06 = Bluetooth HC-06d [package=THT]
  Arduino_Nano_v3 = Arduino Nano (Rev3.0)
  Q1 = NPN-Transistor [part_number=2N2222A package="TO92 [THT]"]
  R2 = Resistor [tolerance=±5% resistance=220 package=THT]
  LED4_5V = LED - 5mm [color="Green (560nm)" package="5 mm [THT]"]
  C1 = Ceramic Capacitor [capacitance=3.3nF voltage=10V package="200 mil [THT, multilayer]"]
  J1 = male pin header, 2 pins [form="♂ (male)"]
  R1 = Resistor [tolerance=±5% resistance=22 package=THT]
  J2 = male pin header, 2 pins [form="♂ (male)" part_number=7-12V]
  LED1 = LED - 5mm [color="Infrared (940nm)" package="5 mm [THT]"]
  LED2 = LED - 5mm [color="Infrared (940nm)" package="5 mm [THT]"]
  LED3 = LED - 5mm [color="Infrared (940nm)" package="5 mm [THT]"]

nets:
  5V: HC-05_/_HC-06.VCC, Arduino_Nano_v3.5V, J1.pin2, R1.Pin_0
  GND: HC-05_/_HC-06.GND, Arduino_Nano_v3.GND, Q1.E, R2.Pin_0, J2.pin2
  N1: HC-05_/_HC-06.TXD, Arduino_Nano_v3.D10
  N2: HC-05_/_HC-06.RXD, Arduino_Nano_v3.D12/MISO
  N3: Arduino_Nano_v3.D2, C1.0
  N4: Arduino_Nano_v3.VIN, J2.pin1
  N5: Q1.B, R2.Pin_1, C1.1
  N6: Q1.C, LED4_5V.cathode, LED3.cathode
  N7: LED4_5V.anode, J1.pin1
  N8: R1.Pin_1, LED1.anode
  N9: LED1.cathode, LED2.anode
  N10: LED2.cathode, LED3.anode

notes:
  david4599 2019
  R2
  R1
  Infrared (940nm)
  furrtek 2014
  Pricehax BT IR Dongle V3.2.0, Bluetooth IR dongle for Pricehax Version 1.1 BT (17.0) furrtek 2014 - david4599 2019

custom parts:
  Bluetooth HC-06d: Bluetooth HC-06 - face down, pins down 16.5mm x 37.5mm PCB
